// Logisim project IT012_Lab01_25521236.circ as structural Verilog: 5 circuits, main circuit TN1
module TN1 (
  input  A,
  input  B,
  input  C,
  output NOT,
  output AND,
  output OR,
  output NAND,
  output NOR,
  output XOR,
  output XNOR,
  output XNOR3,
  output NAND3,
  output CHAIN
);

  wire nand_3_out;

  not not_1 (NOT, A);
  and and_1 (AND, A, B);
  or or_1 (OR, A, B);
  nand nand_1 (NAND, A, B);
  nor nor_1 (NOR, A, B);
  xor xor_1 (XOR, A, B);
  xnor xnor_1 (XNOR, A, B);
  ExactlyOne xor_2 (.out(XNOR3), .in1(A), .in2(B), .in3(C));
  nand nand_2 (NAND3, A, B, C);
  not nand_3 (nand_3_out, A);  // NAND_Gate
  nand nand_4 (CHAIN, nand_3_out, C);
endmodule

module TN2 (
  input  x,
  input  y,
  input  z,
  output EQ1,
  output EQ2,
  output EQ3,
  output EQ4,
  output EQ5
);

  wire not_1_out, not_2_out, not_3_out, x_prime_y_out, x_prime_y_prime_out, x_x_prime_y_out, x_y_2_out,
       x_y___x_z_out, x_y__prime_2_out, x_y__prime_out, x_y_out, x_y_z_out, x_z_out, y_z_out;

  not not_1 (not_1_out, x);
  not not_2 (not_2_out, y);
  and y_z (y_z_out, y, z);
  or x_y (x_y_out, x, y);
  or x_z (x_z_out, x, z);
  not not_3 (not_3_out, x);
  nor x_y__prime (x_y__prime_out, x, y);
  and x_prime_y_prime (x_prime_y_prime_out, not_1_out, not_2_out);
  or x_y_z (x_y_z_out, x, y_z_out);
  nand x_y__prime_2 (x_y__prime_2_out, x, y);
  and x_y___x_z (x_y___x_z_out, x_y_out, x_z_out);
  and x_prime_y (x_prime_y_out, not_3_out, y);
  or x_x_prime_y (x_x_prime_y_out, x, x_prime_y_out);
  xnor xnor_1 (EQ3, x_y_z_out, x_y___x_z_out);
  or x_y_2 (x_y_2_out, x, y);
  xnor xnor_2 (EQ1, x_y__prime_out, x_prime_y_prime_out);
  xnor xnor_3 (EQ2, x_prime_y_prime_out, x_y__prime_2_out);
  xnor xnor_4 (EQ5, x_x_prime_y_out, x_y_2_out);
  xnor xnor_5 (EQ4, x, x_x_prime_y_out);
endmodule

module TN3 (
  input  A,
  input  B,
  input  C,
  input  D,
  output F
);

  wire and_1_out, and_2_out, and_3_out, and_4_out, and_5_out, and_6_out, not_1_out, not_2_out, not_3_out,
       not_4_out;

  not not_1 (not_1_out, A);
  not not_2 (not_2_out, B);
  not not_3 (not_3_out, C);
  not not_4 (not_4_out, D);
  and and_1 (and_1_out, not_1_out, not_2_out, C, not_4_out);
  and and_2 (and_2_out, not_1_out, not_2_out, C, D);
  and and_3 (and_3_out, not_1_out, B, not_3_out, D);
  and and_4 (and_4_out, not_1_out, B, C, D);
  and and_5 (and_5_out, A, not_2_out, C, D);
  and and_6 (and_6_out, A, B, not_3_out, D);
  or or_1 (F, and_1_out, and_2_out, and_3_out, and_4_out, and_5_out, and_6_out);
endmodule

module TN4 (
  input  A,
  input  B,
  input  C,
  input  D,
  output F_CAN,
  output F_SOP,
  output F_POS
);

  wire and_1_out, and_2_out, and_3_out, and_4_out, and_5_out, and_6_out, and_7_out, and_8_out, and_9_out,
       and_10_out, not_1_out, not_2_out, not_3_out, not_4_out, or_1_out, or_2_out, or_3_out, or_4_out;

  not not_1 (not_1_out, A);
  not not_2 (not_2_out, B);
  not not_3 (not_3_out, C);
  not not_4 (not_4_out, D);
  and and_1 (and_1_out, not_1_out, not_2_out, C);
  and and_2 (and_2_out, B, not_3_out, D);
  and and_3 (and_3_out, not_1_out, C, D);
  or or_1 (or_1_out, B, C);
  or or_2 (or_2_out, not_2_out, D);
  or or_3 (or_3_out, not_1_out, D);
  or or_4 (or_4_out, not_1_out, not_2_out, not_3_out);
  and and_4 (and_4_out, not_1_out, not_2_out, C, not_4_out);
  and and_5 (and_5_out, not_1_out, not_2_out, C, D);
  and and_6 (and_6_out, not_1_out, B, not_3_out, D);
  and and_7 (and_7_out, not_1_out, B, C, D);
  and and_8 (and_8_out, A, not_2_out, C, D);
  and and_9 (and_9_out, A, B, not_3_out, D);
  and and_10 (and_10_out, not_2_out, C, D);
  and and_11 (F_POS, or_1_out, or_2_out, or_3_out, or_4_out);
  or or_5 (F_SOP, and_1_out, and_10_out, and_2_out, and_3_out);
  or or_6 (F_CAN, and_4_out, and_5_out, and_6_out, and_7_out, and_8_out, and_9_out);
endmodule

module TN5 (
  input  A,
  input  B,
  input  C,
  output out_4
);

  wire xor_1_out;

  xor xor_1 (xor_1_out, A, B);
  xor xor_2 (out_4, xor_1_out, C);
endmodule
